# Fritzing sketch Pico - RGB Pot (saved by Fritzing 0.9.6b)
breadboards: 1

parts:
  Mod1 = Raspberry Pi Pico
  RGB_LED = RGB LED (com. cathode, rgb) [package="5 mm [THT]"]
  R4 = Resistor [tolerance=±5% resistance=220 package="0805 [SMD]"]
  R5 = Resistor [tolerance=±5% resistance=220 package="0805 [SMD]"]
  R6 = Resistor [tolerance=±5% resistance=220 package="0805 [SMD]"]
  R7 = Rotary Potentiometer (Small) [maximum_resistance=100kΩ package=THT]

nets:
  N1: Mod1.pin_3, Mod1.pin_8, Mod1.pin_13, Mod1.pin_18, Mod1.pin_23, Mod1.pin_28, Mod1.pin_33, Mod1.pin_38, RGB_LED.common_cathode, R7.leg2
  N2: Mod1.pin_17, R4.Pin_0
  N3: Mod1.pin_19, R5.Pin_0
  N4: Mod1.pin_20, R6.Pin_0
  N5: Mod1.pin_31, R7.wiper
  N6: Mod1.pin_36, R7.leg1
  N7: RGB_LED.red_anode, R4.Pin_1
  N8: RGB_LED.green_anode, R5.Pin_1
  N9: RGB_LED.blue_anode, R6.Pin_1

custom parts:
  Raspberry Pi Pico: Raspberry Pi Pico. Based around the RP2040 microcontroller the Pico is a low cost microcontroller device bringing Raspberry Pi quality, cost, and easy of use to the microcontroller space. Jan 2021, Split part in to two versions: tht (this one) and SMD. This one will drill holes for a .1 in header in pcb to allow plugging in the module as well as providing pads to solder the module to the top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
